# Fritzing sketch Wiring (saved by Fritzing 0.9.3b)
# 18650 Li-ion Battery: CC-BY Dr Kristofer Chan, King's College London/Remote-research.org
breadboards: 2

parts:
  GSM_SIM_GPSR_SMS_SIM900_SIM1 = SIM800L [package=THT]
  A1 = u-blox NEO-6M GPS Breakout
  C1 = Capacitor Polarized [package=cpol-radial-10uf-25v]
  C2 = Capacitor Polarized [package=cpol-radial-10uf-25v]
  U2 = ESP8266 NodeMCU LoLin module
  BAT1 = 18650 Li-ion Battery [package=battery-18650]
  BAT2 = 18650 Li-ion Battery [package=battery-18650]
  Mod1 = 2S-BMS
  MOD2 = MT3608 Boost No usb
  M1 = RioRand LM2596
  M2 = RioRand LM2596
  Part1 = Solar Cell
  Part2 = Solar Cell

nets:
  5V: GSM_SIM_GPSR_SMS_SIM900_SIM1.5V, GSM_SIM_GPSR_SMS_SIM900_SIM1.VDD, C2.+, M1.Pin_3
  N1: GSM_SIM_GPSR_SMS_SIM900_SIM1.GND#1, U2.GND, BAT1.-, Mod1.pin2, M1.Pin_2, M2.Pin_2, M2.Pin_4
  N2: GSM_SIM_GPSR_SMS_SIM900_SIM1.SIM_TXD, U2.D5
  N3: GSM_SIM_GPSR_SMS_SIM900_SIM1.SIM_RXD, U2.D6
  N4: GSM_SIM_GPSR_SMS_SIM900_SIM1.GND#5, C2.-
  N5: A1.Pin_1, C1.+
  N6: A1.Pin_2, C1.-
  N7: A1.Pin_3, U2.D3
  N8: A1.Pin_4, U2.D2
  N9: U2.Vin, M2.Pin_3
  N10: BAT1.+, BAT2.-, Mod1.pin3#4
  N11: BAT2.+, Mod1.pin1, M1.Pin_1
  N12: Mod1.pin3#2, MOD2.IN_(-), MOD2.OUT_(-), Part1.-
  N13: Mod1.pin3#3, MOD2.OUT_(+)
  N14: MOD2.IN_(+), Part2.+
  N15: Part1.+, Part2.-

custom parts:
  ESP8266 NodeMCU LoLin module: ESP8266 based NodeMCU
  18650 Li-ion Battery: 18650 li-ion Battery Standard 18650 battery with interactive connectors Creative Common Attribution 4.0 International (CC-BY 4.0) license. Any use of this part requires attribution of Dr Kristofer Chan, Department of Geography, King's College London. Contact kristofer.chan [at] kcl.ac.uk OR kris [at] remote-research.org for further information.
  2S-BMS: 2S-BMS LIPO battery charger / protection unit. Note pcb does not match the board as it will likely connect with wires, so pcb is 5 pads suitable for .1in header pins.
  MT3608 Boost No usb: Chip- MT3608 / B6289 DC to DC step up, power booster module. With adjustable output voltage. Current- 2A . || Input voltage- 2V-24V || Output voltage- 5V-28V Input interface- Inversed polarity- NO. || Led indicator- No.
